// Digital circuit eater_8bit_relay.dig as structural Verilog
module eater_8bit_relay (
  input  clk,
  input  HALT,
  input  in_3,
  input  clk_2,
  input  clk_3,
  input  in_6,
  input  clk_4,
  input  MANUAL,
  input  in_9,
  input  in_10,
  input  in_11,
  input  in_12,
  input  in_13,
  input  in_14,
  input  in_15,
  input  in_16,
  input  SELECT,
  input  in_18,
  input  in_19,
  input  in_20,
  input  in_21,
  input  in_22,
  input  in_23,
  input  in_24,
  input  in_25,
  input  in_26,
  input  [7:0] _1,
  input  in_28,
  input  in_29,
  input  in_30,
  input  [2:0] in_31,
  input  [2:0] in_32
);

  wire and_1_out, and_2_out, B_SIGN, CARRY, CLOCK, not_1_out, relay_1_p3, relay_1_p4, relay_2_p2, relay_3_p3,
       relay_3_p4, relay_4_p2, relay_5_p2, relay_6_p2, relay_7_p4, relay_8_p4, relay_9_p4, relay_10_p4,
       relay_11_p4, relay_12_p4, relay_13_p4, relay_14_p4, relay_15_p4, relay_16_p4, relay_17_p4,
       relay_18_p4, relay_22_p3, relay_22_p4, relay_23_p2, relay_24_p2, relay_25_p4, relaydt_1_p7,
       relaydt_1_p8, relaydt_2_p6, relaydt_2_p7, relaydt_4_p5, relaydt_4_p6, relaydt_6_p2, relaydt_24_p1,
       relaydt_24_p4, relaydt_24_p6, relaydt_26_p1, relaydt_26_p4, relaydt_26_p6, relaydt_27_p3,
       relaydt_27_p6, relaydt_27_p9, relaydt_27_p12, relaydt_27_p17, relaydt_29_p1, relaydt_29_p4,
       relaydt_29_p5, relaydt_29_p7, relaydt_29_p8, relaydt_29_p10, relaydt_30_p1, relaydt_30_p4,
       relaydt_30_p5, relaydt_30_p7, relaydt_30_p8, relaydt_30_p10, relaydt_31_p6, relaydt_31_p7,
       relaydt_32_p2, relaydt_33_p1, relaydt_33_p2, relaydt_34_p1, relaydt_34_p2, relaydt_36_p3,
       relaydt_36_p6, relaydt_36_p9, relaydt_36_p14, relaydt_39_p4, relaydt_39_p6, relaydt_41_p4,
       relaydt_41_p6, relaydt_42_p3, relaydt_43_p1, relaydt_43_p4, relaydt_43_p5, relaydt_43_p7,
       relaydt_43_p8, relaydt_43_p10, relaydt_44_p1, relaydt_44_p4, relaydt_44_p5, relaydt_44_p7,
       relaydt_44_p8, relaydt_44_p10, relaydt_45_p3, relaydt_45_p6, relaydt_45_p9, relaydt_45_p14,
       relaydt_48_p4, relaydt_48_p6, relaydt_49_p1, relaydt_49_p2, relaydt_51_p4, relaydt_51_p6,
       relaydt_52_p1, relaydt_52_p2, relaydt_53_p3, relaydt_54_p1, relaydt_54_p4, relaydt_54_p5,
       relaydt_54_p7, relaydt_54_p8, relaydt_54_p10, relaydt_55_p1, relaydt_55_p4, relaydt_55_p5,
       relaydt_55_p7, relaydt_55_p8, relaydt_55_p10, relaydt_56_p3, relaydt_56_p6, relaydt_56_p9,
       relaydt_56_p14, relaydt_58_p1, relaydt_58_p2, relaydt_59_p1, relaydt_59_p2, relaydt_60_p6,
       relaydt_63_p4, relaydt_63_p6, relaydt_65_p4, relaydt_65_p6, relaydt_66_p6, relaydt_68_p1,
       relaydt_68_p4, relaydt_68_p5, relaydt_68_p7, relaydt_68_p8, relaydt_68_p10, relaydt_69_p1,
       relaydt_69_p4, relaydt_69_p5, relaydt_69_p7, relaydt_69_p8, relaydt_69_p10, relaydt_71_p3,
       relaydt_71_p6, relaydt_71_p9, relaydt_71_p14, relaydt_73_p6, relaydt_75_p1, relaydt_75_p2,
       relaydt_76_p1, relaydt_76_p2, relaydt_77_p6, relaydt_79_p4, relaydt_79_p6, relaydt_81_p4,
       relaydt_81_p6, relaydt_82_p6, relaydt_84_p3, relaydt_84_p6, relaydt_84_p9, relaydt_84_p14,
       relaydt_86_p1, relaydt_86_p4, relaydt_86_p5, relaydt_86_p7, relaydt_86_p8, relaydt_86_p10,
       relaydt_87_p1, relaydt_87_p4, relaydt_87_p5, relaydt_87_p7, relaydt_87_p8, relaydt_87_p10,
       relaydt_88_p6, relaydt_91_p1, relaydt_91_p2, relaydt_92_p1, relaydt_92_p2, relaydt_93_p6,
       relaydt_95_p3, relaydt_95_p6, relaydt_95_p9, relaydt_95_p14, relaydt_98_p4, relaydt_98_p6,
       relaydt_100_p4, relaydt_100_p6, relaydt_102_p1, relaydt_102_p4, relaydt_102_p5, relaydt_102_p7,
       relaydt_102_p8, relaydt_102_p10, relaydt_103_p1, relaydt_103_p4, relaydt_103_p5, relaydt_103_p7,
       relaydt_103_p8, relaydt_103_p10, relaydt_104_p3, relaydt_104_p6, relaydt_104_p9, relaydt_107_p4,
       relaydt_107_p6, relaydt_108_p1, relaydt_108_p2, relaydt_110_p4, relaydt_110_p6, relaydt_111_p1,
       relaydt_111_p2, relaydt_112_p1, relaydt_112_p4, relaydt_112_p5, relaydt_112_p7, relaydt_112_p8,
       relaydt_112_p10, relaydt_113_p1, relaydt_113_p4, relaydt_113_p5, relaydt_113_p7, relaydt_113_p8,
       relaydt_113_p10, relaydt_114_p4, relaydt_114_p5, relaydt_115_p5, relaydt_115_p6, relaydt_115_p7,
       relaydt_115_p8, relaydt_116_p11, relaydt_116_p12, relaydt_116_p13, relaydt_116_p14, relaydt_117_p1,
       relaydt_117_p2, relaydt_118_p1, relaydt_118_p2, relaydt_119_p7, relaydt_119_p8, relaydt_119_p9,
       relaydt_119_p10, relaydt_119_p11, relaydt_119_p12, relaydt_119_p13, relaydt_119_p14, relaydt_120_p2,
       relaydt_120_p3, relaydt_120_p4, relaydt_120_p5, relaydt_122_p4, relaydt_122_p6, relaydt_124_p4,
       relaydt_124_p6, relaydt_125_p1, relaydt_125_p5, relaydt_125_p6, relaydt_125_p8, relaydt_126_p1,
       relaydt_126_p5, relaydt_126_p6, relaydt_126_p8, relaydt_127_p1, relaydt_127_p2, relaydt_128_p1,
       relaydt_128_p2, rs_ff_1_nq, rs_ff_1_q, STEP_out, ZERO;
  wire [0:0] relaydt_37_p14, relaydt_46_p3, relaydt_46_p6, relaydt_46_p9, relaydt_46_p14, relaydt_57_p3,
       relaydt_57_p6, relaydt_57_p9, relaydt_57_p14, relaydt_58_p11, relaydt_59_p11, relaydt_61_p1,
       relaydt_72_p3, relaydt_72_p6, relaydt_72_p9, relaydt_72_p14, relaydt_74_p1, relaydt_75_p11,
       relaydt_76_p11, relaydt_83_p1, relaydt_85_p3, relaydt_85_p6, relaydt_85_p9, relaydt_85_p14,
       relaydt_89_p1, relaydt_90_p1, relaydt_91_p11, relaydt_92_p11, relaydt_94_p1, relaydt_96_p3,
       relaydt_96_p6, relaydt_96_p9, relaydt_96_p14, relaydt_105_p3, relaydt_105_p6, relaydt_105_p10,
       relaydt_108_p11, relaydt_111_p11, relaydt_117_p11, relaydt_118_p11, relaydt_127_p11, relaydt_128_p11;
  wire [1:0] relaydt_28_p3, relaydt_28_p6, relaydt_28_p9, relaydt_28_p12, relaydt_33_p11, relaydt_34_p11,
       relaydt_67_p1;
  wire [6:0] REG_B;
  wire [7:0] BUS, REG_C;

  // Relay relay_1: pin names not known; wires that end beside it: CLOCK, in_20, relay_1_p3, relay_1_p4, 1'b0
  // Relay relay_2: pin names not known; wires that end beside it: BUS[7], relay_2_p2
  // Relay relay_3: pin names not known; wires that end beside it: CLOCK, in_19, relay_3_p3, relay_3_p4, 1'b0
  // Relay relay_4: pin names not known; wires that end beside it: BUS[7], relay_4_p2
  // RelayDT #(.poles(2)) relaydt_1: pin names not known; wires that end beside it: in_6, clk_3, clk_2, clk, clk_4, 1'b0, relaydt_1_p7, relaydt_1_p8, in_3, relaydt_1_p7, relaydt_1_p8
  // RelayDT #(.poles(2)) relaydt_2: pin names not known; wires that end beside it: 1'b0, relay_1_p3, 1'b1, relay_2_p2, 1'b0, relaydt_2_p6, relaydt_2_p7, 1'b0, relaydt_2_p6, 1'b0
  // RelayDT #(.poles(2)) relaydt_3: pin names not known; wires that end beside it: relay_2_p2, B_SIGN, 1'b0, relaydt_2_p7, 1'b1, 1'b0
  LED led_1 (.in(B_SIGN));
  // RelayDT #(.poles(2)) relaydt_4: pin names not known; wires that end beside it: 1'b0, relay_3_p3, 1'b1, relay_4_p2, relaydt_4_p5, relaydt_4_p6, 1'b0, relaydt_4_p5, 1'b0
  // RelayDT #(.poles(2)) relaydt_5: pin names not known; wires that end beside it: relay_4_p2, REG_C[7], relaydt_4_p6, 1'b1, 1'b0
  LED led_2 (.in(REG_C[7]));
  // RelayDT relaydt_6: pin names not known; wires that end beside it: 1'b0, relaydt_6_p2
  // RelayDT relaydt_7: pin names not known; wires that end beside it: 1'b1, relay_1_p4, relay_1_p4, 1'b0
  // RelayDT relaydt_8: pin names not known; wires that end beside it: 1'b1, relay_3_p4, relay_3_p4, 1'b0
  Button STEP (.out(STEP_out));
  and and_1 (and_1_out, STEP_out, MANUAL, ~HALT);  // And
  RS_FF rs_ff_1 (.S(and_2_out), .C(relaydt_6_p2), .R(~and_2_out), .Q(rs_ff_1_q), .nQ(rs_ff_1_nq));
  // Relay relay_5: pin names not known; wires that end beside it: BUS[6], relay_5_p2
  LED led_3 (.in(REG_B[6]));
  // Relay relay_6: pin names not known; wires that end beside it: BUS[6], relay_6_p2
  LED led_4 (.in(REG_C[6]));
  or or_1 (CLOCK, and_1_out, rs_ff_1_q);
  and and_2 (and_2_out, ~MANUAL, ~HALT, rs_ff_1_nq);  // And
  // RelayDT #(.poles(2)) relaydt_9: pin names not known; wires that end beside it: relay_5_p2, relay_5_p2, REG_B[6], 1'b0, relaydt_2_p7, 1'b1, 1'b0
  // RelayDT #(.poles(2)) relaydt_10: pin names not known; wires that end beside it: relay_6_p2, relay_6_p2, REG_C[6], 1'b0, relaydt_4_p6, 1'b1, 1'b0
  not not_1 (not_1_out, CLOCK);
  // Relay relay_7: pin names not known; wires that end beside it: relay_1_p4, BUS[5], 1'b0, relay_7_p4
  // Relay relay_8: pin names not known; wires that end beside it: relay_3_p4, BUS[5], 1'b0, relay_8_p4
  LED led_5 (.in(CLOCK));
  LED led_6 (.in(not_1_out));
  // RelayDT #(.poles(2)) relaydt_11: pin names not known; wires that end beside it: relay_7_p4, relay_7_p4, REG_B[5], 1'b0, relaydt_2_p7, 1'b1, 1'b0
  LED led_7 (.in(REG_B[5]));
  // RelayDT #(.poles(2)) relaydt_12: pin names not known; wires that end beside it: relay_8_p4, relay_8_p4, REG_C[5], 1'b0, relaydt_4_p6, 1'b1, 1'b0
  LED led_8 (.in(REG_C[5]));
  // Relay relay_9: pin names not known; wires that end beside it: relay_1_p4, BUS[4], 1'b0, relay_9_p4
  LED led_9 (.in(REG_B[4]));
  // Relay relay_10: pin names not known; wires that end beside it: relay_3_p4, BUS[4], 1'b0, relay_10_p4
  LED led_10 (.in(REG_C[4]));
  // RelayDT #(.poles(2)) relaydt_13: pin names not known; wires that end beside it: relay_9_p4, relay_9_p4, REG_B[4], 1'b0, relaydt_2_p7, 1'b1, 1'b0
  // RelayDT #(.poles(2)) relaydt_14: pin names not known; wires that end beside it: relay_10_p4, relay_10_p4, REG_C[4], 1'b0, relaydt_4_p6, 1'b1, 1'b0
  // Relay relay_11: pin names not known; wires that end beside it: relay_1_p4, BUS[3], 1'b0, relay_11_p4
  // Relay relay_12: pin names not known; wires that end beside it: relay_3_p4, BUS[3], 1'b0, relay_12_p4
  // RelayDT #(.poles(2)) relaydt_15: pin names not known; wires that end beside it: relay_11_p4, relay_11_p4, REG_B[3], 1'b0, relaydt_2_p7, 1'b1, 1'b0
  LED led_11 (.in(REG_B[3]));
  // RelayDT #(.poles(2)) relaydt_16: pin names not known; wires that end beside it: relay_12_p4, relay_12_p4, REG_C[3], 1'b0, relaydt_4_p6, 1'b1, 1'b0
  LED led_12 (.in(REG_C[3]));
  // Relay relay_13: pin names not known; wires that end beside it: relay_1_p4, BUS[2], 1'b0, relay_13_p4
  LED led_13 (.in(REG_B[2]));
  // Relay relay_14: pin names not known; wires that end beside it: relay_3_p4, BUS[2], 1'b0, relay_14_p4
  LED led_14 (.in(REG_C[2]));
  // RelayDT #(.poles(2)) relaydt_17: pin names not known; wires that end beside it: relay_13_p4, relay_13_p4, REG_B[2], 1'b0, relaydt_2_p7, 1'b1, 1'b0
  // RelayDT #(.poles(2)) relaydt_18: pin names not known; wires that end beside it: relay_14_p4, relay_14_p4, REG_C[2], 1'b0, relaydt_4_p6, 1'b1, 1'b0
  // Relay relay_15: pin names not known; wires that end beside it: relay_1_p4, BUS[1], 1'b0, relay_15_p4
  // Relay relay_16: pin names not known; wires that end beside it: relay_3_p4, BUS[1], 1'b0, relay_16_p4
  // RelayDT #(.poles(2)) relaydt_19: pin names not known; wires that end beside it: relay_15_p4, relay_15_p4, REG_B[1], 1'b0, relaydt_2_p7, 1'b1, 1'b0
  LED led_15 (.in(REG_B[1]));
  // RelayDT #(.poles(2)) relaydt_20: pin names not known; wires that end beside it: relay_16_p4, relay_16_p4, REG_C[1], 1'b0, relaydt_4_p6, 1'b1, 1'b0
  LED led_16 (.in(REG_C[1]));
  // Relay relay_17: pin names not known; wires that end beside it: relay_1_p4, BUS[0], 1'b0, relay_17_p4
  LED led_17 (.in(REG_B[0]));
  // Relay relay_18: pin names not known; wires that end beside it: relay_3_p4, BUS[0], 1'b0, relay_18_p4
  LED led_18 (.in(REG_C[0]));
  // RelayDT #(.poles(2)) relaydt_21: pin names not known; wires that end beside it: relay_17_p4, relay_17_p4, REG_B[0], 1'b0, relaydt_2_p7, 1'b1, 1'b0
  // RelayDT #(.poles(2)) relaydt_22: pin names not known; wires that end beside it: relay_18_p4, relay_18_p4, REG_C[0], 1'b0, relaydt_4_p6, 1'b1, 1'b0
  // Relay #(.Bits(8)) relay_19: pin names not known; wires that end beside it: in_21, {B_SIGN, REG_B}, 1'b0, BUS
  // Relay #(.Bits(8)) relay_20: pin names not known; wires that end beside it: in_18, REG_C, 1'b0, BUS
  LED led_19 (.in(BUS[7]));
  LED led_20 (.in(BUS[6]));
  LED led_21 (.in(BUS[5]));
  // Relay #(.Bits(8)) relay_21: pin names not known; wires that end beside it: SELECT, {in_16, in_15, in_14, in_13, in_12, in_11, in_10, in_9}, 1'b0
  LED led_22 (.in(BUS[4]));
  LED led_23 (.in(BUS[3]));
  LED led_24 (.in(BUS[2]));
  LED led_25 (.in(BUS[1]));
  LED led_26 (.in(BUS[0]));
  LED led_27 (.in(relaydt_28_p3[1]));
  or or_2 (CARRY, relaydt_26_p1, relaydt_24_p1);
  LED led_28 (.in(relaydt_28_p9[1]));
  LED led_29 (.in(relaydt_28_p6[1]));
  // RelayDT relaydt_23: pin names not known; wires that end beside it: 1'b0, 1'b1, 1'b0
  // RelayDT relaydt_24: pin names not known; wires that end beside it: relaydt_24_p1, 1'b0, 1'b1, relaydt_24_p4, relaydt_24_p4, relaydt_24_p6
  // RelayDT relaydt_25: pin names not known; wires that end beside it: 1'b0, 1'b1, 1'b0
  // RelayDT relaydt_26: pin names not known; wires that end beside it: relaydt_26_p1, 1'b0, 1'b1, relaydt_26_p4, relaydt_26_p4, relaydt_26_p6
  // Relay relay_22: pin names not known; wires that end beside it: CLOCK, in_28, relay_22_p3, relay_22_p4, 1'b0
  // RelayDT #(.poles(4)) relaydt_27: pin names not known; wires that end beside it: 1'b0, 1'b1, relaydt_27_p3, 1'b1, 1'b0, relaydt_27_p6, 1'b0, 1'b1, relaydt_27_p9, 1'b0, 1'b1, relaydt_27_p12, REG_C[7], 1'b0, 1'b0, 1'b1, relaydt_27_p17
  // RelayDT #(.poles(4)) relaydt_28: pin names not known; wires that end beside it: 1'b0, relaydt_27_p3, relaydt_28_p3[1], 1'b1, 1'b0, relaydt_28_p6[1], relaydt_27_p9, relaydt_27_p6, relaydt_28_p9[1], relaydt_27_p12, 1'b1, relaydt_28_p12[1], B_SIGN, 1'b0, 1'b0, relaydt_27_p17, relaydt_28_p3[0]
  LED led_30 (.in(relaydt_28_p12[1]));
  // RelayDT #(.poles(4)) relaydt_29: pin names not known; wires that end beside it: relaydt_29_p1, REG_C[7], relaydt_29_p1, relaydt_29_p4, relaydt_29_p5, 1'b0, relaydt_29_p7, relaydt_29_p8, relaydt_24_p6, relaydt_29_p10, relaydt_29_p10, relaydt_29_p7, relaydt_29_p8
  // RelayDT #(.poles(4)) relaydt_30: pin names not known; wires that end beside it: relaydt_30_p1, _1[7], relaydt_30_p1, relaydt_30_p4, relaydt_30_p5, 1'b0, relaydt_30_p7, relaydt_30_p8, relaydt_26_p6, relaydt_30_p10, relaydt_30_p10, relaydt_30_p7, relaydt_30_p8
  // Relay relay_23: pin names not known; wires that end beside it: B_SIGN, relay_23_p2
  LED led_31 (.in(relaydt_28_p3[0]));
  // RelayDT #(.poles(2)) relaydt_31: pin names not known; wires that end beside it: 1'b0, relay_22_p3, 1'b1, relay_23_p2, 1'b0, relaydt_31_p6, relaydt_31_p7, 1'b0, relaydt_31_p6, 1'b0
  // RelayDT #(.poles(2)) relaydt_32: pin names not known; wires that end beside it: relay_23_p2, relaydt_32_p2, relaydt_31_p7, 1'b1, 1'b0
  LED Sign (.in(relaydt_32_p2));
  LED led_32 (.in(relaydt_28_p9[0]));
  LED led_33 (.in(relaydt_28_p6[0]));
  // RelayDT #(.poles(4)) relaydt_33: pin names not known; wires that end beside it: relaydt_33_p1, relaydt_33_p2, relaydt_24_p6, relaydt_29_p10, relaydt_29_p8, relaydt_33_p1, relaydt_33_p1, relaydt_33_p2, 1'b0, relaydt_29_p4, relaydt_33_p11[1], 1'b1, relaydt_29_p5, B_SIGN, 1'b0
  LED led_34 (.in(relaydt_33_p11[1]));
  // RelayDT #(.poles(4)) relaydt_34: pin names not known; wires that end beside it: relaydt_34_p1, relaydt_34_p2, relaydt_26_p6, relaydt_30_p10, relaydt_30_p8, relaydt_34_p1, relaydt_34_p1, relaydt_34_p2, 1'b0, relaydt_30_p4, relaydt_34_p11[1], 1'b1, relaydt_30_p5, B_SIGN, 1'b0
  LED led_35 (.in(relaydt_34_p11[1]));
  // RelayDT relaydt_35: pin names not known; wires that end beside it: 1'b1, relay_22_p4, relay_22_p4, 1'b0
  // Relay relay_24: pin names not known; wires that end beside it: CARRY, relay_24_p2
  // RelayDT #(.poles(4)) relaydt_36: pin names not known; wires that end beside it: 1'b1, 1'b0, relaydt_36_p3, 1'b0, 1'b1, relaydt_36_p6, 1'b0, 1'b1, relaydt_36_p9, REG_C[6], 1'b0, 1'b0, 1'b1, relaydt_36_p14
  // RelayDT #(.poles(4)) relaydt_37: pin names not known; wires that end beside it: 1'b1, 1'b0, relaydt_28_p6[0], relaydt_36_p6, relaydt_36_p3, relaydt_28_p9[0], relaydt_36_p9, 1'b1, relaydt_28_p12[0], REG_B[6], 1'b0, 1'b0, relaydt_36_p14, relaydt_37_p14[0]
  LED led_36 (.in(relaydt_28_p12[0]));
  // RelayDT relaydt_38: pin names not known; wires that end beside it: relaydt_29_p4, 1'b1, 1'b0
  // RelayDT relaydt_39: pin names not known; wires that end beside it: relaydt_29_p5, 1'b0, 1'b1, relaydt_39_p4, relaydt_39_p4, relaydt_39_p6
  // RelayDT relaydt_40: pin names not known; wires that end beside it: relaydt_30_p4, 1'b1, 1'b0
  // RelayDT relaydt_41: pin names not known; wires that end beside it: relaydt_30_p5, 1'b0, 1'b1, relaydt_41_p4, relaydt_41_p4, relaydt_41_p6
  // RelayDT #(.poles(2)) relaydt_42: pin names not known; wires that end beside it: relay_24_p2, relay_24_p2, relaydt_42_p3, 1'b0, relaydt_31_p7, 1'b1, 1'b0
  LED u_Carry (.in(relaydt_42_p3));
  LED led_37 (.in(relaydt_37_p14[0]));
  // RelayDT #(.poles(4)) relaydt_43: pin names not known; wires that end beside it: relaydt_43_p1, REG_C[6], relaydt_43_p1, relaydt_43_p4, relaydt_43_p5, 1'b0, relaydt_43_p7, relaydt_43_p8, relaydt_39_p6, relaydt_43_p10, relaydt_43_p10, relaydt_43_p7, relaydt_43_p8
  // RelayDT #(.poles(4)) relaydt_44: pin names not known; wires that end beside it: relaydt_44_p1, _1[6], relaydt_44_p1, relaydt_44_p4, relaydt_44_p5, 1'b0, relaydt_44_p7, relaydt_44_p8, relaydt_41_p6, relaydt_44_p10, relaydt_44_p10, relaydt_44_p7, relaydt_44_p8
  LED led_38 (.in(relaydt_46_p6[0]));
  LED led_39 (.in(relaydt_46_p3[0]));
  // Relay relay_25: pin names not known; wires that end beside it: relay_22_p4, ZERO, 1'b0, relay_25_p4
  // RelayDT #(.poles(4)) relaydt_45: pin names not known; wires that end beside it: 1'b1, 1'b0, relaydt_45_p3, 1'b0, 1'b1, relaydt_45_p6, 1'b0, 1'b1, relaydt_45_p9, REG_C[5], 1'b0, 1'b0, 1'b1, relaydt_45_p14
  // RelayDT #(.poles(4)) relaydt_46: pin names not known; wires that end beside it: 1'b1, 1'b0, relaydt_46_p3[0], relaydt_45_p6, relaydt_45_p3, relaydt_46_p6[0], relaydt_45_p9, 1'b1, relaydt_46_p9[0], REG_B[5], 1'b0, 1'b0, relaydt_45_p14, relaydt_46_p14[0]
  LED led_40 (.in(relaydt_46_p9[0]));
  // RelayDT relaydt_47: pin names not known; wires that end beside it: relaydt_43_p4, 1'b1, 1'b0
  // RelayDT relaydt_48: pin names not known; wires that end beside it: relaydt_43_p5, 1'b0, 1'b1, relaydt_48_p4, relaydt_48_p4, relaydt_48_p6
  // RelayDT #(.poles(4)) relaydt_49: pin names not known; wires that end beside it: relaydt_49_p1, relaydt_49_p2, relaydt_39_p6, relaydt_43_p10, relaydt_43_p8, relaydt_49_p1, relaydt_49_p1, relaydt_49_p2, 1'b0, relaydt_43_p4, relaydt_33_p11[0], 1'b1, relaydt_43_p5, REG_B[6], 1'b0
  LED led_41 (.in(relaydt_33_p11[0]));
  // RelayDT relaydt_50: pin names not known; wires that end beside it: relaydt_44_p4, 1'b1, 1'b0
  // RelayDT relaydt_51: pin names not known; wires that end beside it: relaydt_44_p5, 1'b0, 1'b1, relaydt_51_p4, relaydt_51_p4, relaydt_51_p6
  // RelayDT #(.poles(4)) relaydt_52: pin names not known; wires that end beside it: relaydt_52_p1, relaydt_52_p2, relaydt_41_p6, relaydt_44_p10, relaydt_44_p8, relaydt_52_p1, relaydt_52_p1, relaydt_52_p2, 1'b0, relaydt_44_p4, relaydt_34_p11[0], 1'b1, relaydt_44_p5, REG_B[6], 1'b0
  LED led_42 (.in(relaydt_34_p11[0]));
  // RelayDT #(.poles(2)) relaydt_53: pin names not known; wires that end beside it: relay_25_p4, relay_25_p4, relaydt_53_p3, 1'b0, relaydt_31_p7, 1'b1, 1'b0
  LED u_Zero (.in(relaydt_53_p3));
  LED led_43 (.in(relaydt_46_p14[0]));
  // RelayDT #(.poles(4)) relaydt_54: pin names not known; wires that end beside it: relaydt_54_p1, REG_C[5], relaydt_54_p1, relaydt_54_p4, relaydt_54_p5, 1'b0, relaydt_54_p7, relaydt_54_p8, relaydt_48_p6, relaydt_54_p10, relaydt_54_p10, relaydt_54_p7, relaydt_54_p8
  // RelayDT #(.poles(4)) relaydt_55: pin names not known; wires that end beside it: relaydt_55_p1, _1[5], relaydt_55_p1, relaydt_55_p4, relaydt_55_p5, 1'b0, relaydt_55_p7, relaydt_55_p8, relaydt_51_p6, relaydt_55_p10, relaydt_55_p10, relaydt_55_p7, relaydt_55_p8
  LED led_44 (.in(relaydt_57_p6[0]));
  LED led_45 (.in(relaydt_57_p3[0]));
  // RelayDT #(.poles(4)) relaydt_56: pin names not known; wires that end beside it: 1'b1, 1'b0, relaydt_56_p3, 1'b0, 1'b1, relaydt_56_p6, 1'b0, 1'b1, relaydt_56_p9, REG_C[4], 1'b0, 1'b0, 1'b1, relaydt_56_p14
  // RelayDT #(.poles(4)) relaydt_57: pin names not known; wires that end beside it: 1'b1, 1'b0, relaydt_57_p3[0], relaydt_56_p6, relaydt_56_p3, relaydt_57_p6[0], relaydt_56_p9, 1'b1, relaydt_57_p9[0], REG_B[4], 1'b0, 1'b0, relaydt_56_p14, relaydt_57_p14[0]
  LED led_46 (.in(relaydt_57_p9[0]));
  // RelayDT #(.poles(4)) relaydt_58: pin names not known; wires that end beside it: relaydt_58_p1, relaydt_58_p2, relaydt_48_p6, relaydt_54_p10, relaydt_54_p8, relaydt_58_p1, relaydt_58_p1, relaydt_58_p2, 1'b0, relaydt_54_p4, relaydt_58_p11[0], 1'b1, relaydt_54_p5, REG_B[5], 1'b0
  // RelayDT #(.poles(4)) relaydt_59: pin names not known; wires that end beside it: relaydt_59_p1, relaydt_59_p2, relaydt_51_p6, relaydt_55_p10, relaydt_55_p8, relaydt_59_p1, relaydt_59_p1, relaydt_59_p2, 1'b0, relaydt_55_p4, relaydt_59_p11[0], 1'b1, relaydt_55_p5, REG_B[5], 1'b0
  // RelayDT relaydt_60: pin names not known; wires that end beside it: B_SIGN, 1'b0, 1'b1, B_SIGN, 1'b0, relaydt_60_p6, 1'b0
  // RelayDT relaydt_61: pin names not known; wires that end beside it: relaydt_61_p1[0], 1'b1, 1'b0
  LED led_47 (.in(relaydt_67_p1[1]));
  LED led_48 (.in(relaydt_57_p14[0]));
  // RelayDT relaydt_62: pin names not known; wires that end beside it: relaydt_54_p4, 1'b1, 1'b0
  // RelayDT relaydt_63: pin names not known; wires that end beside it: relaydt_54_p5, 1'b0, 1'b1, relaydt_63_p4, relaydt_63_p4, relaydt_63_p6
  LED led_49 (.in(relaydt_58_p11[0]));
  // RelayDT relaydt_64: pin names not known; wires that end beside it: relaydt_55_p4, 1'b1, 1'b0
  // RelayDT relaydt_65: pin names not known; wires that end beside it: relaydt_55_p5, 1'b0, 1'b1, relaydt_65_p4, relaydt_65_p4, relaydt_65_p6
  LED led_50 (.in(relaydt_59_p11[0]));
  // RelayDT relaydt_66: pin names not known; wires that end beside it: REG_B[6], 1'b0, relaydt_60_p6, REG_B[6], 1'b0, relaydt_66_p6, 1'b0
  // RelayDT relaydt_67: pin names not known; wires that end beside it: relaydt_67_p1[1], 1'b1, 1'b0
  LED led_51 (.in(relaydt_67_p1[0]));
  LED led_52 (.in(relaydt_72_p6[0]));
  LED led_53 (.in(relaydt_72_p3[0]));
  // RelayDT #(.poles(4)) relaydt_68: pin names not known; wires that end beside it: relaydt_68_p1, REG_C[4], relaydt_68_p1, relaydt_68_p4, relaydt_68_p5, 1'b0, relaydt_68_p7, relaydt_68_p8, relaydt_63_p6, relaydt_68_p10, relaydt_68_p10, relaydt_68_p7, relaydt_68_p8
  // RelayDT #(.poles(4)) relaydt_69: pin names not known; wires that end beside it: relaydt_69_p1, _1[4], relaydt_69_p1, relaydt_69_p4, relaydt_69_p5, 1'b0, relaydt_69_p7, relaydt_69_p8, relaydt_65_p6, relaydt_69_p10, relaydt_69_p10, relaydt_69_p7, relaydt_69_p8
  // RelayDT relaydt_70: pin names not known; wires that end beside it: relaydt_67_p1[0], 1'b1, 1'b0
  LED led_54 (.in(relaydt_74_p1[0]));
  // RelayDT #(.poles(4)) relaydt_71: pin names not known; wires that end beside it: 1'b1, 1'b0, relaydt_71_p3, 1'b0, 1'b1, relaydt_71_p6, 1'b0, 1'b1, relaydt_71_p9, REG_C[3], 1'b0, 1'b0, 1'b1, relaydt_71_p14
  // RelayDT #(.poles(4)) relaydt_72: pin names not known; wires that end beside it: 1'b1, 1'b0, relaydt_72_p3[0], relaydt_71_p6, relaydt_71_p3, relaydt_72_p6[0], relaydt_71_p9, 1'b1, relaydt_72_p9[0], REG_B[3], 1'b0, 1'b0, relaydt_71_p14, relaydt_72_p14[0]
  LED led_55 (.in(relaydt_72_p9[0]));
  // RelayDT relaydt_73: pin names not known; wires that end beside it: REG_B[5], 1'b0, relaydt_66_p6, REG_B[5], 1'b0, relaydt_73_p6, 1'b0
  // RelayDT relaydt_74: pin names not known; wires that end beside it: relaydt_74_p1[0], 1'b1, 1'b0
  LED led_56 (.in(relaydt_72_p14[0]));
  // RelayDT #(.poles(4)) relaydt_75: pin names not known; wires that end beside it: relaydt_75_p1, relaydt_75_p2, relaydt_63_p6, relaydt_68_p10, relaydt_68_p8, relaydt_75_p1, relaydt_75_p1, relaydt_75_p2, 1'b0, relaydt_68_p4, relaydt_75_p11[0], 1'b1, relaydt_68_p5, REG_B[4], 1'b0
  // RelayDT #(.poles(4)) relaydt_76: pin names not known; wires that end beside it: relaydt_76_p1, relaydt_76_p2, relaydt_65_p6, relaydt_69_p10, relaydt_69_p8, relaydt_76_p1, relaydt_76_p1, relaydt_76_p2, 1'b0, relaydt_69_p4, relaydt_76_p11[0], 1'b1, relaydt_69_p5, REG_B[4], 1'b0
  // RelayDT relaydt_77: pin names not known; wires that end beside it: REG_B[4], 1'b0, relaydt_73_p6, REG_B[4], 1'b0, relaydt_77_p6, 1'b0
  LED led_57 (.in(relaydt_83_p1[0]));
  LED led_58 (.in(relaydt_85_p6[0]));
  LED led_59 (.in(relaydt_85_p3[0]));
  // RelayDT relaydt_78: pin names not known; wires that end beside it: relaydt_68_p4, 1'b1, 1'b0
  // RelayDT relaydt_79: pin names not known; wires that end beside it: relaydt_68_p5, 1'b0, 1'b1, relaydt_79_p4, relaydt_79_p4, relaydt_79_p6
  LED led_60 (.in(relaydt_75_p11[0]));
  // RelayDT relaydt_80: pin names not known; wires that end beside it: relaydt_69_p4, 1'b1, 1'b0
  // RelayDT relaydt_81: pin names not known; wires that end beside it: relaydt_69_p5, 1'b0, 1'b1, relaydt_81_p4, relaydt_81_p4, relaydt_81_p6
  LED led_61 (.in(relaydt_76_p11[0]));
  // RelayDT relaydt_82: pin names not known; wires that end beside it: REG_B[3], 1'b0, relaydt_77_p6, REG_B[3], 1'b0, relaydt_82_p6, 1'b0
  // RelayDT relaydt_83: pin names not known; wires that end beside it: relaydt_83_p1[0], 1'b1, 1'b0
  LED led_62 (.in(relaydt_89_p1[0]));
  // RelayDT #(.poles(4)) relaydt_84: pin names not known; wires that end beside it: 1'b1, 1'b0, relaydt_84_p3, 1'b0, 1'b1, relaydt_84_p6, 1'b0, 1'b1, relaydt_84_p9, REG_C[2], 1'b0, 1'b0, 1'b1, relaydt_84_p14
  // RelayDT #(.poles(4)) relaydt_85: pin names not known; wires that end beside it: 1'b1, 1'b0, relaydt_85_p3[0], relaydt_84_p6, relaydt_84_p3, relaydt_85_p6[0], relaydt_84_p9, 1'b1, relaydt_85_p9[0], REG_B[2], 1'b0, 1'b0, relaydt_84_p14, relaydt_85_p14[0]
  LED led_63 (.in(relaydt_85_p9[0]));
  // RelayDT #(.poles(4)) relaydt_86: pin names not known; wires that end beside it: relaydt_86_p1, REG_C[3], relaydt_86_p1, relaydt_86_p4, relaydt_86_p5, 1'b0, relaydt_86_p7, relaydt_86_p8, relaydt_79_p6, relaydt_86_p10, relaydt_86_p10, relaydt_86_p7, relaydt_86_p8
  // RelayDT #(.poles(4)) relaydt_87: pin names not known; wires that end beside it: relaydt_87_p1, _1[3], relaydt_87_p1, relaydt_87_p4, relaydt_87_p5, 1'b0, relaydt_87_p7, relaydt_87_p8, relaydt_81_p6, relaydt_87_p10, relaydt_87_p10, relaydt_87_p7, relaydt_87_p8
  // RelayDT relaydt_88: pin names not known; wires that end beside it: REG_B[2], 1'b0, relaydt_82_p6, REG_B[2], 1'b0, relaydt_88_p6, 1'b0
  // RelayDT relaydt_89: pin names not known; wires that end beside it: relaydt_89_p1[0], 1'b1, 1'b0
  LED led_64 (.in(relaydt_90_p1[0]));
  LED led_65 (.in(relaydt_85_p14[0]));
  // RelayDT relaydt_90: pin names not known; wires that end beside it: relaydt_90_p1[0], 1'b1, 1'b0
  LED led_66 (.in(relaydt_94_p1[0]));
  LED led_67 (.in(relaydt_96_p6[0]));
  LED led_68 (.in(relaydt_96_p3[0]));
  // RelayDT #(.poles(4)) relaydt_91: pin names not known; wires that end beside it: relaydt_91_p1, relaydt_91_p2, relaydt_79_p6, relaydt_86_p10, relaydt_86_p8, relaydt_91_p1, relaydt_91_p1, relaydt_91_p2, 1'b0, relaydt_86_p4, relaydt_91_p11[0], 1'b1, relaydt_86_p5, REG_B[3], 1'b0
  LED led_69 (.in(relaydt_91_p11[0]));
  // RelayDT #(.poles(4)) relaydt_92: pin names not known; wires that end beside it: relaydt_92_p1, relaydt_92_p2, relaydt_81_p6, relaydt_87_p10, relaydt_87_p8, relaydt_92_p1, relaydt_92_p1, relaydt_92_p2, 1'b0, relaydt_87_p4, relaydt_92_p11[0], 1'b1, relaydt_87_p5, REG_B[3], 1'b0
  LED led_70 (.in(relaydt_92_p11[0]));
  // RelayDT relaydt_93: pin names not known; wires that end beside it: REG_B[1], 1'b0, relaydt_88_p6, REG_B[1], 1'b0, relaydt_93_p6, 1'b0
  // RelayDT relaydt_94: pin names not known; wires that end beside it: relaydt_94_p1[0], 1'b1, 1'b0
  // RelayDT #(.poles(4)) relaydt_95: pin names not known; wires that end beside it: 1'b1, 1'b0, relaydt_95_p3, 1'b0, 1'b1, relaydt_95_p6, 1'b0, 1'b1, relaydt_95_p9, REG_C[1], 1'b0, 1'b0, 1'b1, relaydt_95_p14
  // RelayDT #(.poles(4)) relaydt_96: pin names not known; wires that end beside it: 1'b1, 1'b0, relaydt_96_p3[0], relaydt_95_p6, relaydt_95_p3, relaydt_96_p6[0], relaydt_95_p9, 1'b1, relaydt_96_p9[0], REG_B[1], 1'b0, 1'b0, relaydt_95_p14, relaydt_96_p14[0]
  LED led_71 (.in(relaydt_96_p9[0]));
  // RelayDT relaydt_97: pin names not known; wires that end beside it: relaydt_86_p4, 1'b1, 1'b0
  // RelayDT relaydt_98: pin names not known; wires that end beside it: relaydt_86_p5, 1'b0, 1'b1, relaydt_98_p4, relaydt_98_p4, relaydt_98_p6
  // RelayDT relaydt_99: pin names not known; wires that end beside it: relaydt_87_p4, 1'b1, 1'b0
  // RelayDT relaydt_100: pin names not known; wires that end beside it: relaydt_87_p5, 1'b0, 1'b1, relaydt_100_p4, relaydt_100_p4, relaydt_100_p6
  // RelayDT relaydt_101: pin names not known; wires that end beside it: REG_B[0], 1'b0, relaydt_93_p6, REG_B[0], 1'b0, ZERO, 1'b0
  LED led_72 (.in(relaydt_61_p1[0]));
  LED led_73 (.in(relaydt_96_p14[0]));
  // RelayDT #(.poles(4)) relaydt_102: pin names not known; wires that end beside it: relaydt_102_p1, REG_C[2], relaydt_102_p1, relaydt_102_p4, relaydt_102_p5, 1'b0, relaydt_102_p7, relaydt_102_p8, relaydt_98_p6, relaydt_102_p10, relaydt_102_p10, relaydt_102_p7, relaydt_102_p8
  // RelayDT #(.poles(4)) relaydt_103: pin names not known; wires that end beside it: relaydt_103_p1, _1[2], relaydt_103_p1, relaydt_103_p4, relaydt_103_p5, 1'b0, relaydt_103_p7, relaydt_103_p8, relaydt_100_p6, relaydt_103_p10, relaydt_103_p10, relaydt_103_p7, relaydt_103_p8
  // Relay #(.Bits(8)) relay_26: pin names not known; wires that end beside it: in_30, {relaydt_67_p1, relaydt_74_p1[0], relaydt_83_p1[0], relaydt_89_p1[0], relaydt_90_p1[0], relaydt_94_p1[0], relaydt_61_p1[0]}, 1'b0, BUS
  LED led_74 (.in(relaydt_105_p6[0]));
  LED led_75 (.in(relaydt_105_p3[0]));
  // Relay #(.Bits(8)) relay_27: pin names not known; wires that end beside it: in_22, {relaydt_28_p3, relaydt_37_p14[0], relaydt_46_p14[0], relaydt_57_p14[0], relaydt_72_p14[0], relaydt_85_p14[0], relaydt_96_p14[0]}, BUS
  // RelayDT #(.poles(4)) relaydt_104: pin names not known; wires that end beside it: 1'b1, 1'b0, relaydt_104_p3, 1'b0, 1'b1, relaydt_104_p6, 1'b0, 1'b1, relaydt_104_p9, REG_C[0], 1'b0
  // RelayDT #(.poles(4)) relaydt_105: pin names not known; wires that end beside it: 1'b1, 1'b0, relaydt_105_p3[0], relaydt_104_p6, relaydt_104_p3, relaydt_105_p6[0], relaydt_104_p9, 1'b0, 1'b1, relaydt_105_p10[0], REG_B[0], 1'b0, in_23, 1'b0
  LED led_76 (.in(relaydt_105_p10[0]));
  // RelayDT relaydt_106: pin names not known; wires that end beside it: relaydt_102_p4, 1'b1, 1'b0
  // RelayDT relaydt_107: pin names not known; wires that end beside it: relaydt_102_p5, 1'b0, 1'b1, relaydt_107_p4, relaydt_107_p4, relaydt_107_p6
  // RelayDT #(.poles(4)) relaydt_108: pin names not known; wires that end beside it: relaydt_108_p1, relaydt_108_p2, relaydt_98_p6, relaydt_102_p10, relaydt_102_p8, relaydt_108_p1, relaydt_108_p1, relaydt_108_p2, 1'b0, relaydt_102_p4, relaydt_108_p11[0], 1'b1, relaydt_102_p5, REG_B[2], 1'b0
  LED led_77 (.in(relaydt_108_p11[0]));
  // RelayDT relaydt_109: pin names not known; wires that end beside it: relaydt_103_p4, 1'b1, 1'b0
  // RelayDT relaydt_110: pin names not known; wires that end beside it: relaydt_103_p5, 1'b0, 1'b1, relaydt_110_p4, relaydt_110_p4, relaydt_110_p6
  // RelayDT #(.poles(4)) relaydt_111: pin names not known; wires that end beside it: relaydt_111_p1, relaydt_111_p2, relaydt_100_p6, relaydt_103_p10, relaydt_103_p8, relaydt_111_p1, relaydt_111_p1, relaydt_111_p2, 1'b0, relaydt_103_p4, relaydt_111_p11[0], 1'b1, relaydt_103_p5, REG_B[2], 1'b0
  LED led_78 (.in(relaydt_111_p11[0]));
  // Relay #(.Bits(8)) relay_28: pin names not known; wires that end beside it: {relaydt_28_p12, relaydt_46_p9[0], relaydt_57_p9[0], relaydt_72_p9[0], relaydt_85_p9[0], relaydt_96_p9[0], relaydt_105_p10[0]}, in_24, BUS, 1'b0
  // Relay #(.Bits(8)) relay_29: pin names not known; wires that end beside it: {relaydt_28_p9, relaydt_46_p6[0], relaydt_57_p6[0], relaydt_72_p6[0], relaydt_85_p6[0], relaydt_96_p6[0], relaydt_105_p6[0]}, in_25, BUS, 1'b0
  // Relay #(.Bits(8)) relay_30: pin names not known; wires that end beside it: {relaydt_28_p6, relaydt_46_p3[0], relaydt_57_p3[0], relaydt_72_p3[0], relaydt_85_p3[0], relaydt_96_p3[0], relaydt_105_p3[0]}, BUS
  // RelayDT #(.poles(4)) relaydt_112: pin names not known; wires that end beside it: relaydt_112_p1, REG_C[1], relaydt_112_p1, relaydt_112_p4, relaydt_112_p5, 1'b0, relaydt_112_p7, relaydt_112_p8, relaydt_107_p6, relaydt_112_p10, relaydt_112_p10, relaydt_112_p7, relaydt_112_p8
  // RelayDT #(.poles(4)) relaydt_113: pin names not known; wires that end beside it: relaydt_113_p1, _1[1], relaydt_113_p1, relaydt_113_p4, relaydt_113_p5, 1'b0, relaydt_113_p7, relaydt_113_p8, relaydt_110_p6, relaydt_113_p10, relaydt_113_p10, relaydt_113_p7, relaydt_113_p8
  // RelayDT relaydt_114: pin names not known; wires that end beside it: in_31[2], 1'b1, 1'b0, relaydt_114_p4, relaydt_114_p5
  // RelayDT #(.poles(2)) relaydt_115: pin names not known; wires that end beside it: in_31[1], relaydt_114_p4, relaydt_114_p5, 1'b0, relaydt_115_p5, relaydt_115_p6, relaydt_115_p7, relaydt_115_p8
  // RelayDT #(.poles(4)) relaydt_116: pin names not known; wires that end beside it: in_32[2], 1'b1, 1'b0, 1'b1, 1'b0, 1'b0, 1'b1, 1'b0, 1'b1, 1'b0, relaydt_116_p11, relaydt_116_p12, relaydt_116_p13, relaydt_116_p14, in_32[1], relaydt_116_p11, 1'b0, 1'b0, relaydt_116_p12, relaydt_116_p13, 1'b0, 1'b0, relaydt_116_p14
  // RelayDT #(.poles(4)) relaydt_117: pin names not known; wires that end beside it: relaydt_117_p1, relaydt_117_p2, relaydt_107_p6, relaydt_112_p10, relaydt_112_p8, relaydt_117_p1, relaydt_117_p1, relaydt_117_p2, 1'b0, relaydt_112_p4, relaydt_117_p11[0], 1'b1, relaydt_112_p5, REG_B[1], 1'b0
  // RelayDT #(.poles(4)) relaydt_118: pin names not known; wires that end beside it: relaydt_118_p1, relaydt_118_p2, relaydt_110_p6, relaydt_113_p10, relaydt_113_p8, relaydt_118_p1, relaydt_118_p1, relaydt_118_p2, 1'b0, relaydt_113_p4, relaydt_118_p11[0], 1'b1, relaydt_113_p5, REG_B[1], 1'b0
  // RelayDT #(.poles(4)) relaydt_119: pin names not known; wires that end beside it: in_31[0], relaydt_115_p5, relaydt_115_p6, relaydt_115_p7, relaydt_115_p8, 1'b0, relaydt_119_p7, relaydt_119_p8, relaydt_119_p9, relaydt_119_p10, relaydt_119_p11, relaydt_119_p12, relaydt_119_p13, relaydt_119_p14
  // RelayDT #(.poles(4)) relaydt_120: pin names not known; wires that end beside it: 1'b0, relaydt_120_p2, relaydt_120_p3, relaydt_120_p4, relaydt_120_p5
  // RelayDT relaydt_121: pin names not known; wires that end beside it: relaydt_112_p4, 1'b1, 1'b0
  // RelayDT relaydt_122: pin names not known; wires that end beside it: relaydt_112_p5, 1'b0, 1'b1, relaydt_122_p4, relaydt_122_p4, relaydt_122_p6
  LED led_79 (.in(relaydt_117_p11[0]));
  // RelayDT relaydt_123: pin names not known; wires that end beside it: relaydt_113_p4, 1'b1, 1'b0
  // RelayDT relaydt_124: pin names not known; wires that end beside it: relaydt_113_p5, 1'b0, 1'b1, relaydt_124_p4, relaydt_124_p4, relaydt_124_p6
  LED led_80 (.in(relaydt_118_p11[0]));
  LED led_81 (.in(relaydt_120_p2));
  LED led_82 (.in(relaydt_120_p3));
  LED led_83 (.in(relaydt_120_p4));
  LED led_84 (.in(relaydt_120_p5));
  // RelayDT #(.poles(4)) relaydt_125: pin names not known; wires that end beside it: relaydt_125_p1, REG_C[0], relaydt_125_p1, 1'b0, relaydt_125_p5, relaydt_125_p6, relaydt_122_p6, relaydt_125_p8, relaydt_125_p8, relaydt_125_p5, relaydt_125_p6
  // RelayDT #(.poles(4)) relaydt_126: pin names not known; wires that end beside it: relaydt_126_p1, _1[0], relaydt_126_p1, 1'b0, relaydt_126_p5, relaydt_126_p6, relaydt_124_p6, relaydt_126_p8, relaydt_126_p8, relaydt_126_p5, relaydt_126_p6
  LED led_85 (.in(relaydt_119_p7));
  LED led_86 (.in(relaydt_119_p8));
  LED led_87 (.in(relaydt_119_p9));
  LED led_88 (.in(relaydt_119_p10));
  LED led_89 (.in(relaydt_119_p11));
  LED led_90 (.in(relaydt_119_p12));
  LED led_91 (.in(relaydt_119_p13));
  LED led_92 (.in(relaydt_119_p14));
  // RelayDT #(.poles(4)) relaydt_127: pin names not known; wires that end beside it: relaydt_127_p1, relaydt_127_p2, relaydt_122_p6, relaydt_125_p8, relaydt_125_p6, relaydt_127_p1, relaydt_127_p1, relaydt_127_p2, 1'b0, 1'b1, relaydt_127_p11[0], 1'b1, 1'b0, REG_B[0], in_26, 1'b0
  // RelayDT #(.poles(4)) relaydt_128: pin names not known; wires that end beside it: relaydt_128_p1, relaydt_128_p2, relaydt_124_p6, relaydt_126_p8, relaydt_126_p6, relaydt_128_p1, relaydt_128_p1, relaydt_128_p2, 1'b0, 1'b1, relaydt_128_p11[0], 1'b1, 1'b0, REG_B[0], in_29, 1'b0
  // Relay #(.Bits(8)) relay_31: pin names not known; wires that end beside it: {relaydt_33_p11, relaydt_58_p11[0], relaydt_75_p11[0], relaydt_91_p11[0], relaydt_108_p11[0], relaydt_117_p11[0], relaydt_127_p11[0]}, BUS
  LED led_93 (.in(relaydt_127_p11[0]));
  // Relay #(.Bits(8)) relay_32: pin names not known; wires that end beside it: {relaydt_34_p11, relaydt_59_p11[0], relaydt_76_p11[0], relaydt_92_p11[0], relaydt_111_p11[0], relaydt_118_p11[0], relaydt_128_p11[0]}, BUS
  LED led_94 (.in(relaydt_128_p11[0]));

  // Other names for the same wires on the sheet: REG_B[7] = B_SIGN; AND_E = in_22; INCB_E = in_29; NOTB_E = in_25;
  //   OR_E = in_23; RLB = in_20; RLC = in_19; RSB = in_21; RSC = in_18; SCZL = in_28; SHLB_E = in_30; SUM_E = in_26;
  //   XOR_E = in_24

  // Notes on the sheet:
  //   clk: Hz: 4
  //   clk_2: Hz: 8
  //   clk_3: Hz: 16
  //   clk_4: Hz: 2
  //   _1: default 1
  //   CLOCK
  //   B Register
  //   C Register
  //   ALU-Logic
  //   AND
  //   ALU-Arithmetic
  //   SCZ Register
  //   XOR
  //   NOT_B
  //   OR
  //   SUM
  //   SHL
  //   3-8 Decoder
endmodule
